# Fritzing sketch arduino-pots (saved by Fritzing 0.9.3b)
breadboards: 1

parts:
  R3 = Trimmer Potentiometer [maximum_resistance=10kΩ package=THT]
  Part1 = Arduino Uno (Rev3)
  R4 = Trimmer Potentiometer [maximum_resistance=10kΩ package=THT]

nets:
  N1: R3.leg1, Part1.GND, R4.leg1
  N2: R3.wiper, Part1.A0
  N3: R3.leg2, Part1.5V, R4.leg2
  N4: Part1.A1, R4.wiper
