# Fritzing sketch uart-bus (saved by Fritzing 0.9.3b)
breadboards: 2

parts:
  Part3 = Arduino Uno (Rev3)
  LED3 = LED - 3mm [color="Green (555nm)" package="3 mm [THT]"]
  LED4 = LED - 3mm [color="Red (633nm)" package="3 mm [THT]"]
  R3 = Resistor [tolerance=±5% resistance=220 package=THT]
  R4 = Resistor [tolerance=±5% resistance=220 package=THT]
  Part4 = Arduino Uno (Rev3)
  R5 = Trimmer Potentiometer [maximum_resistance=10kΩ package=THT]
  R6 = Trimmer Potentiometer [maximum_resistance=10kΩ package=THT]

nets:
  N1: Part3.D8, Part4.D9_PWM
  N2: Part3.D9_PWM, Part4.D8
  GND: Part3.GND, LED3.cathode, LED4.cathode, Part4.GND
  N3: Part3.D3_PWM, R3.Pin_0
  N4: Part3.D6_PWM, R4.Pin_0
  N5: LED3.anode, R4.Pin_1
  N6: LED4.anode, R3.Pin_1
  N7: Part4.A0, R5.wiper
  N8: Part4.A1, R6.wiper
  N9: Part4.5V, R6.leg2
