# Fritzing sketch uno-with-strip (saved by Fritzing 0.9.3b)

parts:
  U1 = WS2812 RGB LED strip
  Часть1 = Arduino Uno (Rev3)

nets:
  N1: U1.DIN, Часть1.D4
  GND: U1.GND, Часть1.GND
  VCC: U1.VCC, Часть1.5V

custom parts:
  WS2812 RGB LED strip: WS2812 strip
