# Fritzing sketch circuit (saved by Fritzing 0.9.3b)
breadboards: 1

parts:
  Часть1 = Arduino Uno (Rev3)
  R1 = Resistor [tolerance=±5% resistance=220 package=THT]
  LED1 = LED - 5mm [color="Red (633nm)" package="5 mm [THT]"]
  S1 = Pushbutton [package="[THT]"]
  R2 = Resistor [tolerance=±5% resistance=10k package=THT]

nets:
  N1: Часть1.D11_PWM/MOSI, LED1.anode
  N2: Часть1.D13/SCK, S1.Pin_1, S1.Pin_2, R2.Pin_1
  N3: Часть1.GND, R1.Pin_1, S1.Pin_3, S1.Pin_4
  N4: Часть1.5V, R2.Pin_0
  N5: R1.Pin_0, LED1.cathode
