# Fritzing sketch circuit (saved by Fritzing 0.9.3b)
breadboards: 1

parts:
  Часть1 = Arduino Uno (Rev3)
  R1 = Resistor [tolerance=±5% resistance=220 package=THT]
  LED1 = LED - 5mm [color="Red (633nm)" package="5 mm [THT]"]
  R2 = Trimmer Potentiometer [maximum_resistance=10kΩ package=THT]

nets:
  N1: Часть1.A0, R2.wiper
  N2: Часть1.D11_PWM/MOSI, LED1.anode
  N3: Часть1.5V, R2.leg2
  N4: Часть1.GND, R1.Pin_1, R2.leg1
  N5: R1.Pin_0, LED1.cathode
