# Fritzing sketch circuit (saved by Fritzing 0.9.4)
breadboards: 1

parts:
  Часть1 = Arduino Uno (Rev3)
  J1 = Basic Servo
  S2 = Pushbutton [package="[THT]"]
  R3 = Resistor [tolerance=±5% resistance=10k package=THT]

nets:
  N1: Часть1.D9_PWM, J1.pulse
  N2: Часть1.D13/SCK, S2.Pin_1, S2.Pin_2, R3.Pin_1
  GND: Часть1.GND, J1.gnd, S2.Pin_3, S2.Pin_4
  5V: Часть1.5V, J1.vcc, R3.Pin_0
