# Fritzing sketch i2c-interface (saved by Fritzing 0.9.3b)

parts:
  Часть1 = Arduino Uno (Rev3)
  LCD1 = LCD screen
  LCM1602_IIC2 = LCM1602 IIC [part_number="LCM1602 IIC" chip_label="LCM1602 IIC" package="DIP (Dual Inline) [THT]"]

nets:
  N1: Часть1.A4/SDA, LCM1602_IIC2.SDA
  N2: Часть1.A5/SCL, LCM1602_IIC2.SCL
  5V: Часть1.5V, LCM1602_IIC2.VCC
  GND: Часть1.GND, LCM1602_IIC2.GND
  VSS: LCD1.VSS, LCM1602_IIC2.VSS
  VDD: LCD1.VDD, LCM1602_IIC2.VDD
  N3: LCD1.V0, LCM1602_IIC2.V0
  N4: LCD1.RS, LCM1602_IIC2.RS
  N5: LCD1.R/W, LCM1602_IIC2.RW
  N6: LCD1.E, LCM1602_IIC2.E
  N7: LCD1.DB0, LCM1602_IIC2.D0
  N8: LCD1.DB1, LCM1602_IIC2.D1
  N9: LCD1.DB2, LCM1602_IIC2.D2
  N10: LCD1.DB3, LCM1602_IIC2.D3
  N11: LCD1.DB4, LCM1602_IIC2.D4
  N12: LCD1.DB5, LCM1602_IIC2.D5
  N13: LCD1.DB6, LCM1602_IIC2.D6
  N14: LCD1.DB7, LCM1602_IIC2.D7
  N15: LCD1.LED+, LCM1602_IIC2.A
  N16: LCD1.LED-, LCM1602_IIC2.K

custom parts:
  LCM1602 IIC: I2C-Module to use a 1602 or 2004 LCD on with the wire.h libory Serial LCD Modul
