# Fritzing sketch parallel-interface (saved by Fritzing 0.9.3b)
breadboards: 1

parts:
  Часть1 = Arduino Uno (Rev3)
  LCD1 = LCD screen
  R1 = Trimmer Potentiometer [maximum_resistance=10kΩ package=THT]

nets:
  N1: Часть1.D8, LCD1.E
  N2: Часть1.D3_PWM, LCD1.DB4
  N3: Часть1.D4, LCD1.DB5
  N4: Часть1.D5_PWM, LCD1.DB6
  N5: Часть1.D6_PWM, LCD1.DB7
  N6: Часть1.D7, LCD1.RS
  5V: Часть1.5V, LCD1.VDD, LCD1.LED+, R1.leg1
  GND: Часть1.GND, LCD1.VSS, LCD1.R/W, LCD1.LED-, R1.leg2
  N7: LCD1.V0, R1.wiper
