# Fritzing sketch circuit (saved by Fritzing 0.9.4)
breadboards: 1

parts:
  Часть1 = Arduino Uno (Rev3)
  U1 = TMP36 [package=to-92-kit]
  LCM1602_IIC3 = LCM1602 IIC [part_number="LCM1602 IIC" chip_label="LCM1602 IIC" package="DIP (Dual Inline) [THT]"]
  LCD2 = LCD screen

nets:
  N1: Часть1.A1, U1.VOUT
  N2: Часть1.A4/SDA, LCM1602_IIC3.SDA
  N3: Часть1.A5/SCL, LCM1602_IIC3.SCL
  VCC: Часть1.5V, U1.VCC, LCM1602_IIC3.VCC
  GND: Часть1.GND, U1.GND, LCM1602_IIC3.GND
  VSS: LCM1602_IIC3.VSS, LCD2.VSS
  VDD: LCM1602_IIC3.VDD, LCD2.VDD
  N4: LCM1602_IIC3.V0, LCD2.V0
  N5: LCM1602_IIC3.RS, LCD2.RS
  N6: LCM1602_IIC3.RW, LCD2.R/W
  N7: LCM1602_IIC3.E, LCD2.E
  N8: LCM1602_IIC3.D0, LCD2.DB0
  N9: LCM1602_IIC3.D1, LCD2.DB1
  N10: LCM1602_IIC3.D2, LCD2.DB2
  N11: LCM1602_IIC3.D3, LCD2.DB3
  N12: LCM1602_IIC3.D4, LCD2.DB4
  N13: LCM1602_IIC3.D5, LCD2.DB5
  N14: LCM1602_IIC3.D6, LCD2.DB6
  N15: LCM1602_IIC3.D7, LCD2.DB7
  N16: LCM1602_IIC3.A, LCD2.LED+
  N17: LCM1602_IIC3.K, LCD2.LED-

custom parts:
  LCM1602 IIC: I2C-Module to use a 1602 or 2004 LCD on with the wire.h libory Serial LCD Modul
