# Fritzing sketch circuit (saved by Fritzing 0.9.3b)
breadboards: 1

parts:
  Часть1 = Arduino Uno (Rev3)
  J1 = Basic Servo
  U1 = TMP36 [package=to-92]

nets:
  N1: Часть1.A1, U1.VOUT
  N2: Часть1.D9_PWM, J1.pulse
  VCC: Часть1.5V, J1.vcc, U1.VCC
  GND: Часть1.GND, J1.gnd, U1.GND
