# Fritzing sketch circuit (saved by Fritzing 0.9.3b)
breadboards: 1

parts:
  Часть1 = Arduino Uno (Rev3)
  R1 = Resistor [tolerance=±5% resistance=220 package=THT]
  LED1 = LED - 5mm [color="Red (633nm)" package="5 mm [THT]"]
  LED2 = LED - 5mm [color="Yellow (585nm)" package="5 mm [THT]"]
  R2 = Resistor [tolerance=±5% resistance=220 package=THT]
  LED3 = LED - 5mm [color="Green (555nm)" package="5 mm [THT]"]
  R3 = Resistor [tolerance=±5% resistance=220 package=THT]

nets:
  N1: Часть1.D11_PWM/MOSI, LED1.anode
  N2: Часть1.D12/MISO, LED2.anode
  N3: Часть1.D13/SCK, LED3.anode
  N4: Часть1.GND, R1.Pin_1, R2.Pin_1, R3.Pin_1
  N5: R1.Pin_0, LED1.cathode
  N6: LED2.cathode, R2.Pin_0
  N7: LED3.cathode, R3.Pin_0
